# Fritzing sketch Wire Sketch (saved by Fritzing 0.9.3b)
breadboards: 1

parts:
  Raspberry_Pi_2 = Raspberry Pi 3 [part_number=RPI-3-V1.2]
  LED1 = LED - 3mm [color="Red (633nm)" package="3 mm [THT]"]
  S1 = Momentary Switch [package=ksa_sealed_tac_switch]
  R1 = Resistor [tolerance=±5% resistance=270 package="2010 [SMD]"]
  R2 = Resistor [tolerance=±5% resistance=10k package="2010 [SMD]"]
  TC74 = IC, SIP package, 5 pins [chip_label=TC74]
  R4 = Resistor [tolerance=±5% resistance=10k package="2010 [SMD]"]
  MCP3002 = IC, DIP package, 8 pins [chip_label=MCP]
  R3 = Temperature Sensor (Thermistor) [thermistor_type=NTC package=THT]  # not connected

nets:
  N1: Raspberry_Pi_2.GPIO2, TC74.pin2
  N2: Raspberry_Pi_2.GPIO3, TC74.pin4
  N3: Raspberry_Pi_2.GIPO10, MCP3002.pin5
  N4: Raspberry_Pi_2.GIPO9, MCP3002.pin6
  N5: Raspberry_Pi_2.GIPO11, MCP3002.pin7
  N6: Raspberry_Pi_2.GIPO26, R1.Pin_0
  N7: Raspberry_Pi_2.GIPO16, S1.1, R2.Pin_0
  N8: Raspberry_Pi_2.GND, LED1.cathode, S1.4, TC74.pin3, R4.Pin_0, MCP3002.pin4
  N9: Raspberry_Pi_2.5V, R2.Pin_1, TC74.pin5, MCP3002.pin8
  N10: LED1.anode, R1.Pin_1
  N11: R4.Pin_1, MCP3002.pin2
